# Fritzing sketch robot-plus simple (saved by Fritzing 0.9.3b)
perfboards: 1

parts:
  Composant1 = Arduino Nano (Rev3.0) (ICSP)
  M1 = DC Motor
  R1 = Resistor [tolerance=±5% resistance=1k package="0603 [SMD]"]
  Q1 = NPN-Transistor [package="TO92 [THT]"]
  D1 = Rectifier Diode [part_number=1N4001 package="Melf DO-213 AB [SMD]"]
  C1 = Ceramic Capacitor [capacitance=0.1nF package="1206 [SMD, multilayer]"]
  M2 = DC Motor
  R2 = Resistor [tolerance=±5% resistance=1k package="0603 [SMD]"]
  Q2 = NPN-Transistor [package="TO92 [THT]"]
  D2 = Rectifier Diode [part_number=1N4001 package="Melf DO-213 AB [SMD]"]
  C2 = Ceramic Capacitor [capacitance=0.1nF package="1206 [SMD, multilayer]"]
  VCC1 = Battery block 9V
  R3 = PHOTOCELL [package=photocell]
  R4 = PHOTOCELL [package=photocell]
  R5 = Resistor [tolerance=±5% resistance=10k package="1206 [SMD]"]
  R6 = Resistor [tolerance=±5% resistance=10k package="1206 [SMD]"]
  R7 = Resistor [tolerance=±5% resistance=220 package="1206 [SMD]"]
  R8 = Resistor [tolerance=±5% resistance=220 package="1206 [SMD]"]
  LED1 = LED - 3mm [color="Red (633nm)" package="3 mm [THT]"]
  LED2 = LED - 3mm [color="Red (633nm)" package="3 mm [THT]"]

nets:
  N1: Composant1.D1/TX, R1.Pin_0
  N2: Composant1.GND, Q1.E, Q2.E, VCC1.-, R5.Pin_1, R6.Pin_1, LED1.cathode, LED2.cathode
  N3: Composant1.D2, R2.Pin_0
  N4: Composant1.VIN, VCC1.+
  N5: Composant1.5V, M1.pin_2, D1.cathode, C1.0, M2.pin_2, D2.cathode, C2.0, R3.P$1, R4.P$1, R7.Pin_0, R8.Pin_0
  N6: Composant1.A1, R4.P$2, R6.Pin_0
  N7: Composant1.A0, R3.P$2, R5.Pin_0
  N8: M1.pin_1, Q1.C, D1.anode, C1.1
  N9: R1.Pin_1, Q1.B
  N10: M2.pin_1, Q2.C, D2.anode, C2.1
  N11: R2.Pin_1, Q2.B
  N12: R7.Pin_1, LED1.anode
  N13: R8.Pin_1, LED2.anode
